# Fritzing sketch Final-project ECE 508 (saved by Fritzing 0.9.3b)
breadboards: 1

parts:
  Part1 = Arduino Nano 33 IOT
  Part2 = DHT22 module
  Part3 = HX711 Weighing Sensor Module
  Load_Cell1 = Load Cell - Red/white/black/green

nets:
  N1: Part1.RESET, Part1.A7
  GND: Part1.GND, Part1.D13~, Part2.GND, Part3.GND
  N2: Part1.D2, Part3.DO/RX
  N3: Part1.D3~, Part3.CK/TX
  N4: Part1.D5~, Part2.DATA
  N5: Part1.D11/MOSI, Part1.+5V
  VCC: Part1.VIN, Part2.VCC, Part3.VCC
  N6: Part3.E+, Load_Cell1.wire1
  N7: Part3.E-, Load_Cell1.wire3
  N8: Part3.A+, Load_Cell1.wire4
  N9: Part3.A-, Load_Cell1.wire2

notes:
  Pin Layout for HX711and loadcell
  (Excitation+) E+ or Vcc = Red
  (Excitation-) E-or GND = BLACK
  (Output-/signal-/Amplifier-) A- = WHITE
  (Output+/signal+/Amplifier+) A+ = GREEN
  Pin Layout inbetween Hx711 and Arduino
  Vcc=Red
  GND=Black
  Dout=Yellow
  CLK=Gray
  Pin layout in between DHT 22 and Arduino
  Vcc=Red
  GND=Black
  Dout=Cyan
  ECE 508 Final Project
  Rimi Ghosh

custom parts:
  Arduino Nano 33 IOT: The Arduino Nano 33 IoT is the easiest and cheapest point of entry to enhance existing devices (and creating new ones) to be part of the IoT and designing pico-network applications. Whether you are looking at building a sensor network connected to your office or home router, or if you want to create a BLE device sending data to a cellphone, the Nano 33 IoT is your one-stop-solution for many of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
  Load Cell - Red/white/black/green: A rectangle load cell/weighting pressure Sensor with four wires - Red, white, black, green. Normally corresponding with E+, E-, A+, A- respectively.
